// Digital circuit main.dig as structural Verilog
module main (
);

  wire instruction_decoder_1_p1, instruction_decoder_1_p2, instruction_decoder_1_p3,
       instruction_decoder_1_p4, instruction_decoder_1_p6, instruction_decoder_1_p7,
       instruction_decoder_1_p8, instruction_decoder_1_p9, instruction_decoder_1_p10,
       instruction_decoder_1_p11, IR0_q;

  Register IR0 (.D(instruction_decoder_1_p1), .C(instruction_decoder_1_p3), .en(instruction_decoder_1_p4), .Q(IR0_q));
  // instruction_decoder instruction_decoder_1: pin names not known; wires that end beside it: instruction_decoder_1_p1, instruction_decoder_1_p2, instruction_decoder_1_p3, instruction_decoder_1_p4, IR0_q, instruction_decoder_1_p6, instruction_decoder_1_p7, instruction_decoder_1_p8, instruction_decoder_1_p9, instruction_decoder_1_p10, instruction_decoder_1_p11
  Register IR1 (
    .D(instruction_decoder_1_p1), .C(instruction_decoder_1_p7), .en(instruction_decoder_1_p9),
    .Q(instruction_decoder_1_p6));
  Register IR2 (
    .D(instruction_decoder_1_p1), .C(instruction_decoder_1_p10), .en(instruction_decoder_1_p11),
    .Q(instruction_decoder_1_p8));

  // Notes on the sheet:
  //   Instruction Register
endmodule
